// Logisim project rock-paper-scissors-digital-logic.circ as structural Verilog: 6 circuits, main circuit main
module Player1_Decoder (
  input  S1,
  input  S2,
  output out_3,
  output out_4,
  output out_5,
  output out_6
);

  wire not_1_out, not_2_out;

  not not_1 (not_1_out, S1);
  not not_2 (not_2_out, S2);
  and and_1 (out_3, not_1_out, not_2_out);
  and and_2 (out_4, not_1_out, S2);
  and and_3 (out_5, S1, not_2_out);
  and and_4 (out_6, S1, S2);

  // Notes on the sheet:
  //   Player 1 Decoder
  //   Inputs: S1,S2
  //   Outputs: P_Rock, P_Scissors, P_Paper, P_Initial
  //   S1S2: 00=Rock, 01=Scissors, 10=Paper, 11=Initial
  //   P_Rock
  //   P_Scissors
  //   P_Paper
  //   P_Initial
endmodule

module Player2_Decoder (
  input  S3,
  input  S4,
  output out_3,
  output out_4,
  output out_5,
  output out_6
);

  wire not_1_out, not_2_out;

  not not_1 (not_1_out, S3);
  not not_2 (not_2_out, S4);
  and and_1 (out_3, not_1_out, not_2_out);
  and and_2 (out_4, not_1_out, S4);
  and and_3 (out_5, S3, not_2_out);
  and and_4 (out_6, S3, S4);

  // Notes on the sheet:
  //   Player 2 Decoder
  //   Inputs: S3,S4
  //   Outputs: Q_Rock, Q_Scissors, Q_Paper, Q_Initial
  //   S3S4: 00=Rock, 01=Scissors, 10=Paper, 11=Initial
  //   Q_Rock
  //   Q_Scissors
  //   Q_Paper
  //   Q_Initial
endmodule

module P1_Win_Logic (
  input  P_Rock,
  input  Q_Scissors,
  input  P_Scissors,
  input  Q_Paper,
  input  P_Paper,
  input  Q_Rock,
  output P1_Win
);

  wire and_1_out, and_2_out, and_3_out, or_1_out;

  and and_1 (and_1_out, P_Rock, Q_Scissors);
  and and_2 (and_2_out, P_Scissors, Q_Paper);
  and and_3 (and_3_out, P_Paper, Q_Rock);
  or or_1 (or_1_out, and_1_out, and_2_out);
  or or_2 (P1_Win, or_1_out, and_3_out);

  // Notes on the sheet:
  //   Formula:
  //   Player 1 Win Logic
  //   P1 wins when:
  //   Rock beats Scissors, Scissors beats Paper, Paper beats Rock.
  //   P1_Win = (P_Rock.Q_Scissors) + (P_Scissors.Q_Paper) + (P_Paper.Q_Rock)
endmodule

module P2_Win_Logic (
  input  P_Scissors,
  input  Q_Rock,
  input  P_Paper,
  input  Q_Scissors,
  input  P_Rock,
  input  Q_Paper,
  output P2_Win
);

  wire and_1_out, and_2_out, and_3_out, or_1_out;

  and and_1 (and_1_out, P_Scissors, Q_Rock);
  and and_2 (and_2_out, P_Paper, Q_Scissors);
  and and_3 (and_3_out, P_Rock, Q_Paper);
  or or_1 (or_1_out, and_1_out, and_2_out);
  or or_2 (P2_Win, or_1_out, and_3_out);

  // Notes on the sheet:
  //   Formula:
  //   Player 2 Win Logic
  //   P2  wins when:
  //   Rock beats Scissors, Scissors beats Paper, Paper beats Rock.
  //   P2_Win = (P_Scissors.Q_Rock) + (P_Paper.Q_Scissors) + (P_Rock.Q_Paper)
endmodule

module Draw_Logic (
  input  P_Rock,
  input  Q_Rock,
  input  P_Scissors,
  input  Q_Scissors,
  input  P_Paper,
  input  Q_Paper,
  output Draw
);

  wire and_1_out, and_2_out, and_3_out, or_1_out;

  and and_1 (and_1_out, P_Rock, Q_Rock);
  and and_2 (and_2_out, P_Scissors, Q_Scissors);
  and and_3 (and_3_out, P_Paper, Q_Paper);
  or or_1 (or_1_out, and_1_out, and_2_out);
  or or_2 (Draw, or_1_out, and_3_out);

  // Notes on the sheet:
  //   Draw Logic
  //   Formula:
  //   Draw happens when:
  //   Both Players choose Rock, both choose Scissors , or both choose Paper
  //   Draw = (P_Rock.Q_Rock) + (P_Scissors.Q_Scissors) + (P_Paper.Q_Paper)
endmodule

module main (
  input  S1,
  input  S2,
  input  S3,
  input  S4,
  output P1_Win,
  output P2_Win,
  output Draw
);

  wire P_Initial, P_Paper, P_Rock, P_Scissors, Q_Initial, Q_Paper, Q_Rock, Q_Scissors;

  Player1_Decoder player1_decoder_1 (
    .S1(S1), .S2(S2), .out_3(P_Rock), .out_4(P_Scissors), .out_5(P_Paper), .out_6(P_Initial));
  Player2_Decoder player2_decoder_1 (
    .S3(S3), .S4(S4), .out_3(Q_Rock), .out_4(Q_Scissors), .out_5(Q_Paper), .out_6(Q_Initial));
  P1_Win_Logic p1_win_logic_1 (
    .P_Rock(P_Rock), .Q_Scissors(Q_Scissors), .P_Scissors(P_Scissors), .Q_Paper(Q_Paper), .P_Paper(P_Paper),
    .Q_Rock(Q_Rock), .P1_Win(P1_Win));
  P2_Win_Logic p2_win_logic_1 (
    .P_Scissors(P_Scissors), .Q_Rock(Q_Rock), .P_Paper(P_Paper), .Q_Scissors(Q_Scissors), .P_Rock(P_Rock),
    .Q_Paper(Q_Paper), .P2_Win(P2_Win));
  Draw_Logic draw_logic_1 (
    .P_Rock(P_Rock), .Q_Rock(Q_Rock), .P_Scissors(P_Scissors), .Q_Scissors(Q_Scissors), .P_Paper(P_Paper),
    .Q_Paper(Q_Paper), .Draw(Draw));
  LED led_1 (.in(P1_Win));
  LED led_2 (.in(P2_Win));
  LED led_3 (.in(Draw));
endmodule
